# Fritzing sketch final_circuit_strip (saved by Fritzing 0.9.3b)

parts:
  Part7 = Adafruit Perma-Proto HAT [part_number="Adafruit #2314 and #2310"]
  J15 = double row male pin header, 2 pins [form="♂ (male)"]
  J16 = double row male pin header, 2 pins [form="♂ (male)"]
  R7 = Resistor [tolerance=±5% resistance=4.7k package="0402 [SMD]"]

nets:
  N1: Part7.SDA, J15.pin1
  N2: Part7.SCL, J15.pin2
  N3: Part7.3.3V, J16.pin2
  N4: Part7.GND, J16.pin1
  N5: Part7.N$11, R7.Pin_1
  N6: Part7.N$15, R7.Pin_0

custom parts:
  Adafruit Perma-Proto HAT: To kick off the Adafruit HAT party, we have this Perma-Proto inspired plug in daughter board. It has a grid of 0.1" prototyping soldering holes for attaching chips, resistors, LED, potentiometers and more. The holes are connected underneath with traces to mimic the solderless breadboards you're familiar. There's also long power strips for +3V, +5V and Ground connections to the Pi. Near the top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
